// Logisim project alu.circ as structural Verilog: 1 circuit, main circuit main
module main (
  input  [31:0] X,
  input  [31:0] Y,
  input  [3:0] Switch,
  output Signed_Overflow,
  output Equal,
  output [31:0] Result
);

  wire adder_2_cout, adder_3_cout, subtractor_2_bout, subtractor_3_bout, xor_1_out, xor_2_out;
  wire [0:0] comparator_1_lt, comparator_2_lt;
  wire [31:0] adder_1_out, and_1_out, or_1_out, shifter_1_out, shifter_2_out, shifter_3_out, subtractor_1_out;

  Adder #(.width(32)) adder_1 (.a(X), .b(Y), .out(adder_1_out));  // open: cin, cout
  Subtractor #(.width(32)) subtractor_1 (.a(X), .b(Y), .out(subtractor_1_out));  // open: bin, bout
  assign and_1_out = X & Y;  // AND_Gate and_1, 32 bits wide
  assign or_1_out = X | Y;  // OR_Gate or_1, 32 bits wide
  Shifter #(.width(32)) shifter_1 (.in(Y), .\dist (X[4:0]), .out(shifter_1_out));
  Shifter #(.width(32), .shift("lr")) shifter_2 (.in(Y), .\dist (X[4:0]), .out(shifter_2_out));
  Shifter #(.width(32), .shift("ar")) shifter_3 (.in(Y), .\dist (X[4:0]), .out(shifter_3_out));
  Comparator #(.width(32)) comparator_1 (.a(X), .b(Y), .lt(comparator_1_lt[0]));  // open: gt, eq
  Comparator #(.width(32), .mode("unsigned")) comparator_2 (.a(X), .b(Y), .lt(comparator_2_lt[0]));  // open: gt, eq
  Comparator #(.width(32)) comparator_3 (.a(X), .b(Y), .eq(Equal));  // open: gt, lt
  Multiplexer #(.select(4), .width(32)) multiplexer_1 (
    .in0(shifter_1_out), .in1(shifter_2_out), .in2(shifter_3_out), .in3({32{1'b0}}), .in4({32{1'b0}}),
    .in5(adder_1_out), .in6(adder_1_out), .in7(subtractor_1_out), .in8(subtractor_1_out), .in9(and_1_out),
    .in10(or_1_out), .in11({{31{1'b0}}, comparator_1_lt[0]}), .in12({{31{1'b0}}, comparator_2_lt[0]}),
    .in13({32{1'b0}}), .in14({32{1'b0}}), .in15({32{1'b0}}), .out(Result), .sel(Switch));  // open: en
  Adder #(.width(31)) adder_2 (.a(X[30:0]), .b(Y[30:0]), .cout(adder_2_cout));  // open: out, cin
  Adder #(.width(1)) adder_3 (.a(X[31]), .b(Y[31]), .cin(adder_2_cout), .cout(adder_3_cout));  // open: out
  Subtractor #(.width(31)) subtractor_2 (.a(X[30:0]), .b(Y[30:0]), .bout(subtractor_2_bout));  // open: out, bin
  Subtractor #(.width(1)) subtractor_3 (
    .a(X[31]), .b(Y[31]), .bin(subtractor_2_bout), .bout(subtractor_3_bout));  // open: out
  xor xor_1 (xor_1_out, adder_2_cout, adder_3_cout);
  xor xor_2 (xor_2_out, subtractor_2_bout, subtractor_3_bout);
  Multiplexer #(.select(4)) multiplexer_2 (
    .in0(1'b0), .in1(1'b0), .in2(1'b0), .in3(1'b0), .in4(1'b0), .in5(xor_1_out), .in6(1'b0), .in7(xor_2_out),
    .in8(1'b0), .in9(1'b0), .in10(1'b0), .in11(1'b0), .in12(1'b0), .in13(1'b0), .in14(1'b0), .in15(1'b0),
    .out(Signed_Overflow), .sel(Switch));  // open: en

  // Other names for the same wires on the sheet: overflow = Signed_Overflow; S[3:0] = Switch

  // Notes on the sheet:
  //   INPUTS to your circuit
  //   DON'T CHANGE THE LOCATIONS OF THE INPUTS AND OUTPUTS!
  //   OUTPUTS from your circuit
endmodule
