// Logisim project regfile.circ as structural Verilog: 1 circuit, main circuit main
module main (
  input  [4:0] Read_Register_1,
  input  [4:0] Read_Register_2,
  input  [4:0] Write_Register,
  input  [31:0] Write_Data,
  input  Write_Enable,
  input  Clock,
  output [31:0] s0_Value,
  output [31:0] s1_Value,
  output [31:0] s2_Value,
  output [31:0] ra_Value,
  output [31:0] sp_Value,
  output [31:0] Read_Data_1,
  output [31:0] Read_Data_2
);

  wire demultiplexer_1_out1, demultiplexer_1_out2, demultiplexer_1_out3, demultiplexer_1_out4,
       demultiplexer_1_out5, demultiplexer_1_out6, demultiplexer_1_out7, demultiplexer_1_out8,
       demultiplexer_1_out9, demultiplexer_1_out10, demultiplexer_1_out11, demultiplexer_1_out12,
       demultiplexer_1_out13, demultiplexer_1_out14, demultiplexer_1_out15, demultiplexer_1_out16,
       demultiplexer_1_out17, demultiplexer_1_out18, demultiplexer_1_out19, demultiplexer_1_out20,
       demultiplexer_1_out21, demultiplexer_1_out22, demultiplexer_1_out23, demultiplexer_1_out24,
       demultiplexer_1_out25, demultiplexer_1_out26, demultiplexer_1_out27, demultiplexer_1_out28,
       demultiplexer_1_out29, demultiplexer_1_out30, demultiplexer_1_out31;
  wire [31:0] _00_out, _01_out, _02_out, _03_out, _04_out, _05_out, _07_out, _08_out, _09_out, _10_out,
       _11_out, _12_out, _13_out, _14_out, _15_out, _19_out, _20_out, _21_out, _22_out, _23_out, _24_out,
       _25_out, _26_out, _27_out, _28_out, _30_out;

  Multiplexer #(.select(5), .width(32)) multiplexer_1 (
    .in0(_00_out), .in1(_01_out), .in2(_02_out), .in3(_03_out), .in4(_04_out), .in5(_05_out), .in6(_05_out),
    .in7(_07_out), .in8(_08_out), .in9(_09_out), .in10(_10_out), .in11(_11_out), .in12(_12_out),
    .in13(_13_out), .in14(_14_out), .in15(_15_out), .in16(s0_Value), .in17(s1_Value), .in18(s2_Value),
    .in19(_19_out), .in20(_20_out), .in21(_21_out), .in22(_22_out), .in23(_23_out), .in24(_24_out),
    .in25(_25_out), .in26(_26_out), .in27(_27_out), .in28(_28_out), .in29(sp_Value), .in30(_30_out),
    .in31(ra_Value), .out(Read_Data_1), .sel(Read_Register_1));  // open: en
  Multiplexer #(.select(5), .width(32)) multiplexer_2 (
    .in0(_00_out), .in1(_01_out), .in2(_02_out), .in3(_03_out), .in4(_04_out), .in5(_05_out), .in6(_05_out),
    .in7(_07_out), .in8(_08_out), .in9(_09_out), .in10(_10_out), .in11(_11_out), .in12(_12_out),
    .in13(_13_out), .in14(_14_out), .in15(_15_out), .in16(s0_Value), .in17(s1_Value), .in18(s2_Value),
    .in19(_19_out), .in20(_20_out), .in21(_21_out), .in22(_22_out), .in23(_23_out), .in24(_24_out),
    .in25(_25_out), .in26(_26_out), .in27(_27_out), .in28(_28_out), .in29(sp_Value), .in30(_30_out),
    .in31(ra_Value), .out(Read_Data_2), .sel(Read_Register_2));  // open: en
  Demultiplexer #(.select(5)) demultiplexer_1 (
    .out1(demultiplexer_1_out1), .out2(demultiplexer_1_out2), .out3(demultiplexer_1_out3),
    .out4(demultiplexer_1_out4), .out5(demultiplexer_1_out5), .out6(demultiplexer_1_out6),
    .out7(demultiplexer_1_out7), .out8(demultiplexer_1_out8), .out9(demultiplexer_1_out9),
    .out10(demultiplexer_1_out10), .out11(demultiplexer_1_out11), .out12(demultiplexer_1_out12),
    .out13(demultiplexer_1_out13), .out14(demultiplexer_1_out14), .out15(demultiplexer_1_out15),
    .out16(demultiplexer_1_out16), .out17(demultiplexer_1_out17), .out18(demultiplexer_1_out18),
    .out19(demultiplexer_1_out19), .out20(demultiplexer_1_out20), .out21(demultiplexer_1_out21),
    .out22(demultiplexer_1_out22), .out23(demultiplexer_1_out23), .out24(demultiplexer_1_out24),
    .out25(demultiplexer_1_out25), .out26(demultiplexer_1_out26), .out27(demultiplexer_1_out27),
    .out28(demultiplexer_1_out28), .out29(demultiplexer_1_out29), .out30(demultiplexer_1_out30),
    .out31(demultiplexer_1_out31), .in(Write_Enable), .sel(Write_Register));  // open: out0, en
  Register #(.width(32)) zero__00 (.D(Write_Data), .en(1'b0), .Q(_00_out), .clk(Clock));  // open: clr
  Register #(.width(32)) s1___01 (.D(Write_Data), .en(demultiplexer_1_out1), .Q(_01_out), .clk(Clock));  // open: clr
  Register #(.width(32)) v0___02 (.D(Write_Data), .en(demultiplexer_1_out2), .Q(_02_out), .clk(Clock));  // open: clr
  Register #(.width(32)) v1__03 (.D(Write_Data), .en(demultiplexer_1_out3), .Q(_03_out), .clk(Clock));  // open: clr
  Register #(.width(32)) a0___04 (.D(Write_Data), .en(demultiplexer_1_out4), .Q(_04_out), .clk(Clock));  // open: clr
  Register #(.width(32)) a1___05 (.D(Write_Data), .en(demultiplexer_1_out5), .Q(_05_out), .clk(Clock));  // open: clr
  Register #(.width(32)) a2___06 (.D(Write_Data), .en(demultiplexer_1_out6), .Q(_05_out), .clk(Clock));  // open: clr
  Register #(.width(32)) a3___07 (.D(Write_Data), .en(demultiplexer_1_out7), .Q(_07_out), .clk(Clock));  // open: clr
  Register #(.width(32)) t0___08 (.D(Write_Data), .en(demultiplexer_1_out8), .Q(_08_out), .clk(Clock));  // open: clr
  Register #(.width(32)) t1___09 (.D(Write_Data), .en(demultiplexer_1_out9), .Q(_09_out), .clk(Clock));  // open: clr
  Register #(.width(32)) t2___10 (.D(Write_Data), .en(demultiplexer_1_out10), .Q(_10_out), .clk(Clock));  // open: clr
  Register #(.width(32)) t3___11 (.D(Write_Data), .en(demultiplexer_1_out11), .Q(_11_out), .clk(Clock));  // open: clr
  Register #(.width(32)) t4___12 (.D(Write_Data), .en(demultiplexer_1_out12), .Q(_12_out), .clk(Clock));  // open: clr
  Register #(.width(32)) t5__13 (.D(Write_Data), .en(demultiplexer_1_out13), .Q(_13_out), .clk(Clock));  // open: clr
  Register #(.width(32)) t6___14 (.D(Write_Data), .en(demultiplexer_1_out14), .Q(_14_out), .clk(Clock));  // open: clr
  Register #(.width(32)) t7___15 (.D(Write_Data), .en(demultiplexer_1_out15), .Q(_15_out), .clk(Clock));  // open: clr
  Register #(.width(32)) s0___16 (.D(Write_Data), .en(demultiplexer_1_out16), .Q(s0_Value), .clk(Clock));  // open: clr
  Register #(.width(32)) s1___17 (.D(Write_Data), .en(demultiplexer_1_out17), .Q(s1_Value), .clk(Clock));  // open: clr
  Register #(.width(32)) s2___18 (.D(Write_Data), .en(demultiplexer_1_out18), .Q(s2_Value), .clk(Clock));  // open: clr
  Register #(.width(32)) s3___19 (.D(Write_Data), .en(demultiplexer_1_out19), .Q(_19_out), .clk(Clock));  // open: clr
  Register #(.width(32)) s4___20 (.D(Write_Data), .en(demultiplexer_1_out20), .Q(_20_out), .clk(Clock));  // open: clr
  Register #(.width(32)) s5___21 (.D(Write_Data), .en(demultiplexer_1_out21), .Q(_21_out), .clk(Clock));  // open: clr
  Register #(.width(32)) s6___22 (.D(Write_Data), .en(demultiplexer_1_out22), .Q(_22_out), .clk(Clock));  // open: clr
  Register #(.width(32)) s7___23 (.D(Write_Data), .en(demultiplexer_1_out23), .Q(_23_out), .clk(Clock));  // open: clr
  Register #(.width(32)) t8___24 (.D(Write_Data), .en(demultiplexer_1_out24), .Q(_24_out), .clk(Clock));  // open: clr
  Register #(.width(32)) t9___25 (.D(Write_Data), .en(demultiplexer_1_out25), .Q(_25_out), .clk(Clock));  // open: clr
  Register #(.width(32)) k0___26 (.D(Write_Data), .en(demultiplexer_1_out26), .Q(_26_out), .clk(Clock));  // open: clr
  Register #(.width(32)) k1___27 (.D(Write_Data), .en(demultiplexer_1_out27), .Q(_27_out), .clk(Clock));  // open: clr
  Register #(.width(32)) gp___28 (.D(Write_Data), .en(demultiplexer_1_out28), .Q(_28_out), .clk(Clock));  // open: clr
  Register #(.width(32)) sp___29 (.D(Write_Data), .en(demultiplexer_1_out29), .Q(sp_Value), .clk(Clock));  // open: clr
  Register #(.width(32)) s8___30 (.D(Write_Data), .en(demultiplexer_1_out30), .Q(_30_out), .clk(Clock));  // open: clr
  Register #(.width(32)) ra___31 (.D(Write_Data), .en(demultiplexer_1_out31), .Q(ra_Value), .clk(Clock));  // open: clr

  // Other names for the same wires on the sheet: _06_out[31:0] = _05_out; _16_out[31:0] = s0_Value;
  //   _17_out[31:0] = s1_Value; _18_out[31:0] = s2_Value; _29_out[31:0] = sp_Value; _31_out[31:0] = ra_Value;
  //   clk = Clock; read_data1[31:0] = Read_Data_1; read_data2[31:0] = Read_Data_2; read_reg1[4:0] = Read_Register_1;
  //   read_reg2[4:0] = Read_Register_2; write_en = Write_Enable; write_reg[4:0] = Write_Register

  // Notes on the sheet:
  //   INPUTS to your circuit
  //   DON'T CHANGE THE LOCATIONS OF THE INPUTS AND OUTPUTS!
  //   These are DEBUG/TEST outputs from your circuit.
  //   OUTPUTS from your circuit
endmodule
